// Logisim project PC2.circ as structural Verilog
module main (
);

  wire CLK, Reset;
  wire [4:0] driver0, driver1, driver2, driver3, instruction_decoder_2_rd, instruction_decoder_2_rs,
       instruction_decoder_2_rt, instruction_decoder_2_shamt;
  wire [5:0] instruction_decoder_1_funct, instruction_decoder_1_opcode, instruction_decoder_2_funct,
       instruction_decoder_2_opcode;
  wire [6:0] display_driver_1_col0, display_driver_1_col1, display_driver_1_col2, display_driver_1_col3,
       display_driver_1_col4, display_driver_2_col0, display_driver_2_col1, display_driver_2_col2,
       display_driver_2_col3, display_driver_2_col4, display_driver_3_col0, display_driver_3_col1,
       display_driver_3_col2, display_driver_3_col3, display_driver_3_col4, display_driver_4_col0,
       display_driver_4_col1, display_driver_4_col2, display_driver_4_col3, display_driver_4_col4;
  wire [15:0] instruction_decoder_2_immediate;
  wire [23:0] PC;
  wire [25:0] instruction_decoder_2_address;
  wire [31:0] adder_1_out, Curr_Inst, register_1_q;

  Clock clock_1 (.out(CLK));
  Button button_1 (.out(Reset));
  // Probe on PC
  Register #(.width(32)) register_1 (.D(adder_1_out), .en(1'b1), .Q(register_1_q), .clk(CLK), .clr(Reset));
  // Probe on Curr_Inst
  Adder #(.width(32)) adder_1 (.a(32'h1), .b(register_1_q), .out(adder_1_out));  // open: cin, cout
  Bit_Extender #(.in_width(32), .out_width(24)) bit_extender_1 (.in(register_1_q), .out(PC));
  Instruction_Decoder instruction_decoder_1 (
    .Inst(Curr_Inst), .Opcode(instruction_decoder_1_opcode), .funct(instruction_decoder_1_funct));  // open: rs, rt, rd, shamt, Immediate, address
  RAM #(.addrWidth(24), .dataWidth(32)) ram_1 (
    .addr(PC), .data(Curr_Inst), .sel(1'b1), .clk(CLK), .ld(1'b1), .clr(1'b0));
  Debug_Circuit debug_circuit_1 (
    .Funct(instruction_decoder_1_funct), .Opcode(instruction_decoder_1_opcode), .scr3(driver3),
    .scr2(driver2), .scr1(driver1), .scr0(driver0));
  Instruction_Decoder instruction_decoder_2 (
    .Inst(Curr_Inst), .Opcode(instruction_decoder_2_opcode), .rs(instruction_decoder_2_rs),
    .rt(instruction_decoder_2_rt), .rd(instruction_decoder_2_rd), .shamt(instruction_decoder_2_shamt),
    .funct(instruction_decoder_2_funct), .Immediate(instruction_decoder_2_immediate),
    .address(instruction_decoder_2_address));
  DotMatrix dotmatrix_1 (
    .col0(display_driver_1_col0), .col1(display_driver_1_col1), .col2(display_driver_1_col2),
    .col3(display_driver_1_col3), .col4(display_driver_1_col4));
  Display_Driver display_driver_1 (
    .in_1(driver0), .col0(display_driver_1_col0), .col1(display_driver_1_col1), .col2(display_driver_1_col2),
    .col3(display_driver_1_col3), .col4(display_driver_1_col4));
  DotMatrix dotmatrix_2 (
    .col0(display_driver_3_col0), .col1(display_driver_3_col1), .col2(display_driver_3_col2),
    .col3(display_driver_3_col3), .col4(display_driver_3_col4));
  DotMatrix dotmatrix_3 (
    .col0(display_driver_2_col0), .col1(display_driver_2_col1), .col2(display_driver_2_col2),
    .col3(display_driver_2_col3), .col4(display_driver_2_col4));
  Display_Driver display_driver_2 (
    .in_1(driver1), .col0(display_driver_2_col0), .col1(display_driver_2_col1), .col2(display_driver_2_col2),
    .col3(display_driver_2_col3), .col4(display_driver_2_col4));
  Display_Driver display_driver_3 (
    .in_1(driver2), .col0(display_driver_3_col0), .col1(display_driver_3_col1), .col2(display_driver_3_col2),
    .col3(display_driver_3_col3), .col4(display_driver_3_col4));
  DotMatrix dotmatrix_4 (
    .col0(display_driver_4_col0), .col1(display_driver_4_col1), .col2(display_driver_4_col2),
    .col3(display_driver_4_col3), .col4(display_driver_4_col4));
  Display_Driver display_driver_4 (
    .in_1(driver3), .col0(display_driver_4_col0), .col1(display_driver_4_col1), .col2(display_driver_4_col2),
    .col3(display_driver_4_col3), .col4(display_driver_4_col4));
endmodule

module Instruction_Decoder (
  input  [31:0] Inst,
  output [5:0] Opcode,
  output [4:0] rs,
  output [4:0] rt,
  output [4:0] rd,
  output [4:0] shamt,
  output [5:0] funct,
  output [15:0] Immediate,
  output [25:0] address
);


  assign address = Inst[25:0];
  assign funct = Inst[5:0];
  assign Immediate = Inst[15:0];
  assign Opcode = Inst[31:26];
  assign rd = Inst[15:11];
  assign rs = Inst[25:21];
  assign rt = Inst[20:16];
  assign shamt = Inst[10:6];
endmodule

module CU (
  input  [5:0] Opcode,
  output Jump,
  output RegDst,
  output ALUSrc,
  output MemToReg,
  output RegWrite,
  output MemRead,
  output MemWrite,
  output Branch,
  output [1:0] ALUOp
);

  wire comparator_1_eq, comparator_2_eq, comparator_3_eq, comparator_4_eq, comparator_5_eq, comparator_6_eq;

  Comparator #(.width(6)) comparator_1 (.a(Opcode), .b({6{1'b0}}), .eq(comparator_1_eq));  // open: gt, lt
  Comparator #(.width(6)) comparator_2 (.a(Opcode), .b(6'b001000), .eq(comparator_2_eq));  // open: gt, lt
  Comparator #(.width(6)) comparator_3 (.a(Opcode), .b(6'b100011), .eq(comparator_3_eq));  // open: gt, lt
  Comparator #(.width(6)) comparator_4 (.a(Opcode), .b(6'b101011), .eq(comparator_4_eq));  // open: gt, lt
  Comparator #(.width(6)) comparator_5 (.a(Opcode), .b(6'b000100), .eq(comparator_5_eq));  // open: gt, lt
  Comparator #(.width(6)) comparator_6 (.a(Opcode), .b(6'b000010), .eq(comparator_6_eq));  // open: gt, lt
  assign {Jump, RegDst, ALUSrc, MemToReg, RegWrite, MemRead, MemWrite, Branch, ALUOp} = comparator_1_eq ? 10'h1aa : 10'bz;  // Controlled_Buffer controlled_buffer_1
  assign {Jump, RegDst, ALUSrc, MemToReg, RegWrite, MemRead, MemWrite, Branch, ALUOp} = comparator_2_eq ? 10'hc0 : 10'bz;  // Controlled_Buffer controlled_buffer_2
  assign {Jump, RegDst, ALUSrc, MemToReg, RegWrite, MemRead, MemWrite, Branch, ALUOp} = comparator_3_eq ? 10'hf0 : 10'bz;  // Controlled_Buffer controlled_buffer_3
  assign {Jump, RegDst, ALUSrc, MemToReg, RegWrite, MemRead, MemWrite, Branch, ALUOp} = comparator_4_eq ? 10'h88 : 10'bz;  // Controlled_Buffer controlled_buffer_4
  assign {Jump, RegDst, ALUSrc, MemToReg, RegWrite, MemRead, MemWrite, Branch, ALUOp} = comparator_5_eq ? 10'h5 : 10'bz;  // Controlled_Buffer controlled_buffer_5
  assign {Jump, RegDst, ALUSrc, MemToReg, RegWrite, MemRead, MemWrite, Branch, ALUOp} = comparator_6_eq ? 10'h200 : 10'bz;  // Controlled_Buffer controlled_buffer_6

  // Notes on the sheet:
  //   R-Type
  //   Addi
  //   Load
  //   Store
  //   Branch
  //   Jump
endmodule

module Debug_Circuit (
  input  [5:0] Funct,
  input  [5:0] Opcode,
  output [4:0] scr3,
  output [4:0] scr2,
  output [4:0] scr1,
  output [4:0] scr0
);

  wire and_1_out, comparator_1_eq, not_1_out;
  wire [9:0] func_parser_1_add;

  Comparator #(.width(6)) comparator_1 (.a({6{1'b0}}), .b(Opcode), .eq(comparator_1_eq));  // open: gt, lt
  not not_1 (not_1_out, comparator_1_eq);
  func_parser func_parser_1 (
    .in_1(Funct), .Enable(comparator_1_eq), .add(func_parser_1_add[0]), .subs(func_parser_1_add[1]),
    .\and (func_parser_1_add[2]), .\or (func_parser_1_add[3]), .less_than(func_parser_1_add[4]));
  opcode_parser opcode_parser_1 (
    .in_1(Opcode), .Enable(not_1_out), .addi(func_parser_1_add[5]), .load(func_parser_1_add[6]),
    .store(func_parser_1_add[7]), .branch(func_parser_1_add[8]), .jump(func_parser_1_add[9]));
  assign {scr0, scr1, scr2, scr3} = func_parser_1_add[5] ? 20'h9089 : 20'bz;  // Controlled_Buffer controlled_buffer_1
  assign {scr0, scr1, scr2, scr3} = func_parser_1_add[6] ? 20'h63c24 : 20'bz;  // Controlled_Buffer controlled_buffer_2
  assign {scr0, scr1, scr2, scr3} = func_parser_1_add[7] ? 20'h9d1f2 : 20'bz;  // Controlled_Buffer controlled_buffer_3
  assign {scr0, scr1, scr2, scr3} = func_parser_1_add[8] ? 20'h1482e : 20'bz;  // Controlled_Buffer controlled_buffer_4
  assign {scr0, scr1, scr2, scr3} = func_parser_1_add[9] ? 20'h555b0 : 20'bz;  // Controlled_Buffer controlled_buffer_5
  assign {scr0, scr1, scr2, scr3} = func_parser_1_add[0] ? 20'h9080 : 20'bz;  // Controlled_Buffer controlled_buffer_6
  assign {scr0, scr1, scr2, scr3} = func_parser_1_add[1] ? 20'h9d453 : 20'bz;  // Controlled_Buffer controlled_buffer_7
  assign {scr0, scr1, scr2, scr3} = func_parser_1_add[2] ? 20'hb880 : 20'bz;  // Controlled_Buffer controlled_buffer_8
  assign {scr0, scr1, scr2, scr3} = func_parser_1_add[3] ? 20'h7c800 : 20'bz;  // Controlled_Buffer controlled_buffer_9
  assign {scr0, scr1, scr2, scr3} = func_parser_1_add[4] ? 20'h61673 : 20'bz;  // Controlled_Buffer controlled_buffer_10
  and and_1 (and_1_out, ~func_parser_1_add[0], ~func_parser_1_add[1], ~func_parser_1_add[2], ~func_parser_1_add[3], ~func_parser_1_add[4], ~func_parser_1_add[5], ~func_parser_1_add[6], ~func_parser_1_add[7], ~func_parser_1_add[8], ~func_parser_1_add[9]);  // AND_Gate
  assign {scr0, scr1, scr2, scr3} = and_1_out ? 20'h73df0 : 20'bz;  // Controlled_Buffer controlled_buffer_11
endmodule

module func_parser (
  input  [5:0] in_1,
  input  Enable,
  output add,
  output subs,
  output \and ,
  output \or ,
  output less_than
);

  wire and_1_out, and_2_out, and_3_out, and_4_out, and_5_out, not_1_out, not_2_out, not_3_out, not_4_out,
       not_5_out, not_6_out, not_7_out, not_8_out, not_9_out, not_10_out, not_11_out, not_12_out, not_13_out,
       not_14_out, not_15_out, not_16_out, not_17_out, not_18_out, not_19_out;

  not not_1 (not_1_out, in_1[4]);
  not not_2 (not_2_out, in_1[3]);
  not not_3 (not_3_out, in_1[2]);
  not not_4 (not_4_out, in_1[1]);
  not not_5 (not_5_out, in_1[0]);
  not not_6 (not_6_out, in_1[4]);
  not not_7 (not_7_out, in_1[3]);
  not not_8 (not_8_out, in_1[2]);
  not not_9 (not_9_out, in_1[0]);
  not not_10 (not_10_out, in_1[4]);
  not not_11 (not_11_out, in_1[3]);
  not not_12 (not_12_out, in_1[1]);
  not not_13 (not_13_out, in_1[0]);
  not not_14 (not_14_out, in_1[4]);
  not not_15 (not_15_out, in_1[3]);
  not not_16 (not_16_out, in_1[1]);
  not not_17 (not_17_out, in_1[4]);
  not not_18 (not_18_out, in_1[2]);
  not not_19 (not_19_out, in_1[0]);
  and and_1 (and_1_out, in_1[5], not_1_out, not_2_out, not_3_out, not_4_out, not_5_out);
  and and_2 (and_2_out, in_1[5], not_6_out, not_7_out, not_8_out, in_1[1], not_9_out);
  and and_3 (and_3_out, in_1[5], not_10_out, not_11_out, in_1[2], not_12_out, not_13_out);
  and and_4 (and_4_out, in_1[5], not_14_out, not_15_out, in_1[2], not_16_out, in_1[0]);
  and and_5 (and_5_out, in_1[5], not_17_out, in_1[3], not_18_out, in_1[1], not_19_out);
  and and_6 (add, and_1_out, Enable);
  and and_7 (subs, and_2_out, Enable);
  and and_8 (\and , and_3_out, Enable);
  and and_9 (\or , and_4_out, Enable);
  and and_10 (less_than, and_5_out, Enable);
endmodule

module opcode_parser (
  input  [5:0] in_1,
  input  Enable,
  output addi,
  output load,
  output store,
  output branch,
  output jump
);

  wire and_1_out, and_2_out, and_3_out, and_4_out, and_5_out, not_1_out, not_2_out, not_3_out, not_4_out,
       not_5_out, not_6_out, not_7_out, not_8_out, not_9_out, not_10_out, not_11_out, not_12_out, not_13_out,
       not_14_out, not_15_out, not_16_out, not_17_out, not_18_out, not_19_out, not_20_out;

  not not_1 (not_1_out, in_1[5]);
  not not_2 (not_2_out, in_1[4]);
  not not_3 (not_3_out, in_1[2]);
  not not_4 (not_4_out, in_1[1]);
  not not_5 (not_5_out, in_1[0]);
  not not_6 (not_6_out, in_1[4]);
  not not_7 (not_7_out, in_1[3]);
  not not_8 (not_8_out, in_1[2]);
  not not_9 (not_9_out, in_1[4]);
  not not_10 (not_10_out, in_1[2]);
  not not_11 (not_11_out, in_1[5]);
  not not_12 (not_12_out, in_1[4]);
  not not_13 (not_13_out, in_1[3]);
  not not_14 (not_14_out, in_1[1]);
  not not_15 (not_15_out, in_1[0]);
  not not_16 (not_16_out, in_1[5]);
  not not_17 (not_17_out, in_1[4]);
  not not_18 (not_18_out, in_1[3]);
  not not_19 (not_19_out, in_1[2]);
  not not_20 (not_20_out, in_1[0]);
  and and_1 (and_1_out, not_1_out, not_2_out, in_1[3], not_3_out, not_4_out, not_5_out);
  and and_2 (and_2_out, in_1[5], not_6_out, not_7_out, not_8_out, in_1[1], in_1[0]);
  and and_3 (and_3_out, in_1[5], not_9_out, in_1[3], not_10_out, in_1[1], in_1[0]);
  and and_4 (and_4_out, not_11_out, not_12_out, not_13_out, in_1[2], not_14_out, not_15_out);
  and and_5 (and_5_out, not_16_out, not_17_out, not_18_out, not_19_out, in_1[1], not_20_out);
  and and_6 (addi, and_1_out, Enable);
  and and_7 (load, and_2_out, Enable);
  and and_8 (store, and_3_out, Enable);
  buf and_9 (branch, and_4_out);  // AND_Gate
  and and_10 (jump, and_5_out, Enable);
endmodule

module Display_Driver (
  input  [4:0] in_1,
  output [6:0] col0,
  output [6:0] col1,
  output [6:0] col2,
  output [6:0] col3,
  output [6:0] col4
);

  Multiplexer #(.select(5), .width(7)) multiplexer_1 (
    .in0({7{1'b0}}), .in1(7'b0111111), .in2({7{1'b1}}), .in3(7'b0111110), .in4({7{1'b1}}), .in5({7{1'b1}}),
    .in6({7{1'b1}}), .in7(7'b0111110), .in8({7{1'b1}}), .in9(7'b1000001), .in10(7'b1000110),
    .in11({7{1'b1}}), .in12({7{1'b1}}), .in13({7{1'b1}}), .in14({7{1'b1}}), .in15(7'b0111110),
    .in16({7{1'b1}}), .in17(7'b0111110), .in18({7{1'b1}}), .in19(7'b0110001), .in20(7'b1000000),
    .in21(7'b1111110), .in22(7'b1111100), .in23({7{1'b1}}), .in24(7'b1100011), .in25(7'b1110000),
    .in26(7'b1000011), .in27({7{1'b0}}), .in28(7'b0100111), .in29(7'b0100010), .in30(7'b1111000),
    .in31(7'b1111001), .out(col0), .sel(in_1));  // open: en
  Multiplexer #(.select(5), .width(7)) multiplexer_2 (
    .in0({7{1'b0}}), .in1(7'b1000100), .in2(7'b1001001), .in3(7'b1000001), .in4(7'b1000001),
    .in5(7'b1001001), .in6(7'b1001000), .in7(7'b1000001), .in8(7'b0001000), .in9(7'b1000001),
    .in10(7'b1000001), .in11(7'b0001000), .in12(7'b0000001), .in13(7'b0100000), .in14(7'b0100000),
    .in15(7'b1000001), .in16(7'b1001000), .in17(7'b1000001), .in18(7'b1000100), .in19(7'b1001001),
    .in20(7'b1000000), .in21(7'b0000001), .in22(7'b0000010), .in23(7'b0000010), .in24(7'b0010100),
    .in25(7'b0001000), .in26(7'b1000101), .in27(7'b1000001), .in28(7'b1001001), .in29(7'b1000001),
    .in30(7'b0001000), .in31(7'b1001001), .out(col1), .sel(in_1));  // open: en
  Multiplexer #(.select(5), .width(7)) multiplexer_3 (
    .in0({7{1'b0}}), .in1(7'b1000100), .in2(7'b1001001), .in3(7'b1000001), .in4(7'b1000001),
    .in5(7'b1001001), .in6(7'b1001000), .in7(7'b1001001), .in8(7'b0001000), .in9({7{1'b1}}),
    .in10(7'b1000001), .in11(7'b0001000), .in12(7'b0000001), .in13(7'b0011000), .in14(7'b0010000),
    .in15(7'b1000001), .in16(7'b1001000), .in17(7'b1000011), .in18(7'b1000100), .in19(7'b1001001),
    .in20({7{1'b1}}), .in21(7'b0000001), .in22(7'b0000001), .in23(7'b0001100), .in24(7'b0001000),
    .in25(7'b0000111), .in26(7'b1001001), .in27({7{1'b1}}), .in28(7'b1001001), .in29(7'b1001001),
    .in30(7'b0001000), .in31(7'b1001001), .out(col2), .sel(in_1));  // open: en
  Multiplexer #(.select(5), .width(7)) multiplexer_4 (
    .in0({7{1'b0}}), .in1(7'b1000100), .in2(7'b1001001), .in3(7'b1000001), .in4(7'b1000001),
    .in5(7'b1001001), .in6(7'b1000000), .in7(7'b1001001), .in8(7'b0001000), .in9(7'b1000001),
    .in10(7'b1111110), .in11(7'b0010100), .in12(7'b0000001), .in13(7'b0100000), .in14(7'b0001000),
    .in15(7'b1000001), .in16(7'b1001000), .in17(7'b1000001), .in18(7'b1000100), .in19(7'b1001001),
    .in20(7'b1000000), .in21(7'b0000001), .in22(7'b0000010), .in23(7'b0000010), .in24(7'b0010100),
    .in25(7'b0001000), .in26(7'b1010001), .in27(7'b0000001), .in28(7'b1001001), .in29(7'b1001001),
    .in30({7{1'b1}}), .in31(7'b1001001), .out(col3), .sel(in_1));  // open: en
  Multiplexer #(.select(5), .width(7)) multiplexer_5 (
    .in0({7{1'b0}}), .in1(7'b0111111), .in2(7'b0110110), .in3(7'b0100010), .in4(7'b0111110),
    .in5(7'b1001001), .in6(7'b1000000), .in7(7'b0101110), .in8({7{1'b1}}), .in9(7'b1000001),
    .in10(7'b1000000), .in11(7'b1100011), .in12(7'b0000001), .in13({7{1'b1}}), .in14({7{1'b1}}),
    .in15(7'b0111110), .in16(7'b0110000), .in17(7'b0111110), .in18(7'b0111011), .in19(7'b1000110),
    .in20(7'b1000000), .in21(7'b1111110), .in22(7'b1111100), .in23({7{1'b1}}), .in24(7'b1100011),
    .in25(7'b1110000), .in26(7'b1100001), .in27({7{1'b0}}), .in28(7'b0110001), .in29(7'b0110110),
    .in30(7'b0001000), .in31(7'b1000110), .out(col4), .sel(in_1));  // open: en
endmodule
